// Logisim project Circuitos_Combinacionais.circ as structural Verilog: 1 circuit, main circuit main
module main (
  input  A_1,
  input  B_1,
  input  A_2,
  input  B_2
);

  wire and_1_out, and_2_out, and_3_out, not_1_out, not_2_out, or_1_out, or_2_out;

  not not_1 (not_1_out, A_1);
  not not_2 (not_2_out, B_1);
  or or_1 (or_1_out, A_2, B_2);
  LED S_2 (.in(or_1_out));
  and and_1 (and_1_out, A_1, not_2_out);
  and and_2 (and_2_out, not_1_out, B_1);
  and and_3 (and_3_out, A_1, B_1);
  or or_2 (or_2_out, and_1_out, and_2_out, and_3_out);
  LED S_1 (.in(or_2_out));

  // Notes on the sheet:
  //   _
  //   S = A + B
  //   _
  //   S = ( A.B) + (A.B) + (A.B)
endmodule
