// Logisim project Codificador.circ as structural Verilog: 1 circuit, main circuit main
module main (
  input  B1,
  input  B2,
  input  B3,
  input  B4,
  input  B5,
  input  B6,
  input  B7,
  input  B8,
  input  B9
);

  wire [3:0] or_4_out;

  Hex_Digit_Display hex_digit_display_1 (.value(or_4_out));  // open: dp
  or or_1 (or_4_out[3], B9, B8);
  or or_2 (or_4_out[2], B7, B6, B5, B4);
  or or_3 (or_4_out[1], B7, B6, B3, B2);
  or or_4 (or_4_out[0], B9, B7, B5, B3, B1);
  LED b_3 (.in(or_4_out[3]));
  LED b_2 (.in(or_4_out[2]));
  LED b_1 (.in(or_4_out[1]));
  LED b_0 (.in(or_4_out[0]));

  // Notes on the sheet:
  //   CODIFICADOR
endmodule
