// Logisim project Comparador_de_Magnitude.circ as structural Verilog: 3 circuits, main circuit main
module main (
  input  A3,
  input  B3,
  input  A2,
  input  B2,
  input  A1,
  input  B1,
  input  A0,
  input  B0
);

  wire fcom_1_amenorb, fcom_1_out_6, fcom_1_out_7, fcom_2_amenorb, fcom_2_out_6, fcom_2_out_7,
       fcom_3_amenorb, fcom_3_out_6, fcom_3_out_7, hcom_1_aigualb, hcom_1_amaiorb, hcom_1_amenorb;

  HCom hcom_1 (.A0(A0), .B0(B0), .AmaiorB(hcom_1_amaiorb), .AigualB(hcom_1_aigualb), .AmenorB(hcom_1_amenorb));
  FCom fcom_1 (
    .An(A1), .Bn(B1), .aMAIORb(hcom_1_amaiorb), .aIGUALb(hcom_1_aigualb), .in_5(hcom_1_amenorb),
    .out_6(fcom_1_out_6), .out_7(fcom_1_out_7), .AmenorB(fcom_1_amenorb));
  FCom fcom_2 (
    .An(A2), .Bn(B2), .aMAIORb(fcom_1_out_6), .aIGUALb(fcom_1_out_7), .in_5(fcom_1_amenorb),
    .out_6(fcom_2_out_6), .out_7(fcom_2_out_7), .AmenorB(fcom_2_amenorb));
  LED AmaiorB (.in(fcom_3_out_6));
  FCom fcom_3 (
    .An(A3), .Bn(B3), .aMAIORb(fcom_2_out_6), .aIGUALb(fcom_2_out_7), .in_5(fcom_2_amenorb),
    .out_6(fcom_3_out_6), .out_7(fcom_3_out_7), .AmenorB(fcom_3_amenorb));
  LED AigualB (.in(fcom_3_out_7));
  LED AmenorB (.in(fcom_3_amenorb));

  // Notes on the sheet:
  //   COMPARADOR DE MAGNITUDE
endmodule

module HCom (
  input  A0,
  input  B0,
  output AmaiorB,
  output AigualB,
  output AmenorB
);

  wire and_2_out, and_3_out, not_1_out, not_2_out;

  not not_1 (not_1_out, A0);
  not not_2 (not_2_out, B0);
  and and_1 (AmaiorB, A0, not_2_out);
  and and_2 (and_2_out, not_1_out, not_2_out);
  and and_3 (and_3_out, A0, B0);
  and and_4 (AmenorB, not_1_out, B0);
  or or_1 (AigualB, and_2_out, and_3_out);
endmodule

module FCom (
  input  An,
  input  Bn,
  input  aMAIORb,
  input  aIGUALb,
  input  in_5,
  output out_6,
  output out_7,
  output AmenorB
);

  wire and_1_out, and_2_out, and_3_out, and_4_out, and_5_out, and_6_out, and_7_out, and_8_out, and_9_out,
       and_10_out, not_1_out, not_2_out, not_3_out, not_4_out, not_5_out;

  not not_1 (not_1_out, An);
  not not_2 (not_2_out, Bn);
  not not_3 (not_3_out, aMAIORb);
  not not_4 (not_4_out, aIGUALb);
  not not_5 (not_5_out, in_5);
  and and_1 (and_1_out, An, not_2_out, not_3_out, not_4_out, in_5);
  and and_2 (and_2_out, An, not_2_out, not_3_out, aIGUALb, not_5_out);
  and and_3 (and_3_out, not_2_out, aMAIORb, not_4_out, not_5_out);
  and and_4 (and_4_out, An, aMAIORb, not_4_out, not_5_out);
  and and_5 (and_5_out, not_1_out, not_2_out, not_3_out, aIGUALb, not_5_out);
  and and_6 (and_6_out, An, Bn, not_3_out, aIGUALb, not_5_out);
  and and_7 (and_7_out, not_1_out, not_3_out, not_4_out, in_5);
  and and_8 (and_8_out, Bn, not_3_out, not_4_out, in_5);
  and and_9 (and_9_out, not_1_out, Bn, not_3_out, aIGUALb, not_5_out);
  and and_10 (and_10_out, not_1_out, Bn, aMAIORb, not_4_out, not_5_out);
  or or_1 (out_6, and_1_out, and_2_out, and_3_out, and_4_out);
  or or_2 (out_7, and_5_out, and_6_out);
  or or_3 (AmenorB, and_7_out, and_8_out, and_9_out, and_10_out);
endmodule
