// Logisim project Decodificador.circ as structural Verilog: 2 circuits, main circuit main
module main (
  input  A1,
  input  A0,
  input  CS_1,
  input  A_1,
  input  A_0,
  input  CS
);

  wire and_1_out, and_2_out, and_3_out, and_4_out, dec2x4_1_o_0, dec2x4_1_o_1, dec2x4_1_o_2, dec2x4_1_o_3,
       not_1_out, not_2_out;

  not not_1 (not_1_out, A1);
  not not_2 (not_2_out, A0);
  and and_1 (and_1_out, not_1_out, not_2_out, CS);
  and and_2 (and_2_out, not_1_out, A0, CS);
  and and_3 (and_3_out, A1, not_2_out, CS);
  and and_4 (and_4_out, A1, A0, CS);
  LED O0 (.in(and_1_out));
  LED O1 (.in(and_2_out));
  LED O2 (.in(and_3_out));
  LED O3 (.in(and_4_out));
  Dec2x4 dec2x4_1 (
    .CS_1(CS_1), .A_1(A_1), .A_0(A_0), .O_0(dec2x4_1_o_0), .O_1(dec2x4_1_o_1), .O_2(dec2x4_1_o_2),
    .O_3(dec2x4_1_o_3));
  LED led_1 (.in(dec2x4_1_o_0));
  LED led_2 (.in(dec2x4_1_o_1));
  LED led_3 (.in(dec2x4_1_o_2));
  LED led_4 (.in(dec2x4_1_o_3));

  // Notes on the sheet:
  //   DECODIFICADOR: (3x4) ou (2x4+CS)
endmodule

module Dec2x4 (
  input  CS_1,
  input  A_1,
  input  A_0,
  output O_0,
  output O_1,
  output O_2,
  output O_3
);

  wire not_1_out, not_2_out;

  not not_1 (not_1_out, A_1);
  not not_2 (not_2_out, A_0);
  and and_1 (O_0, CS_1, not_1_out, not_2_out);
  and and_2 (O_1, CS_1, not_1_out, A_0);
  and and_3 (O_2, CS_1, A_1, not_2_out);
  and and_4 (O_3, CS_1, A_1, A_0);
endmodule
