// Logisim project EQUIVALENCIA_ENTRE_BLOCOS.circ as structural Verilog: 1 circuit, main circuit main
module main (
  input  E_0,
  input  E_1,
  input  E_2,
  input  E_3,
  input  E_4,
  input  E_5,
  input  E_6,
  input  E_7,
  input  E_8,
  input  E_9,
  input  E_10,
  input  E_11,
  input  E_12,
  input  E_13,
  input  E_14,
  input  E_15,
  input  E_16,
  input  E_17,
  input  E_18
);

  wire and_1_out, and_2_out, nand_1_out, nand_2_out, nand_3_out, nor_1_out, nor_2_out, nor_3_out, not_1_out,
       or_1_out, or_2_out;

  not not_1 (not_1_out, E_0);
  nand nand_1 (nand_1_out, E_1, E_1);
  nor nor_1 (nor_1_out, E_2, E_2);
  and and_1 (and_1_out, E_3, E_4);
  nor nor_2 (nor_2_out, ~E_5, ~E_6);  // NOR_Gate
  nand nand_2 (nand_2_out, E_7, E_8);
  or or_1 (or_1_out, ~E_9, ~E_10);  // OR_Gate
  or or_2 (or_2_out, E_11, E_12);
  nand nand_3 (nand_3_out, ~E_13, ~E_14);  // NAND_Gate
  nor nor_3 (nor_3_out, E_15, E_16);
  and and_2 (and_2_out, ~E_17, ~E_18);  // AND_Gate
  LED S_0 (.in(not_1_out));
  LED S_1 (.in(nand_1_out));
  LED S_2 (.in(nor_1_out));
  LED S_3 (.in(and_1_out));
  LED S_4 (.in(nor_2_out));
  LED S_5 (.in(nand_2_out));
  LED S_6 (.in(or_1_out));
  LED S_7 (.in(or_2_out));
  LED S_8 (.in(nand_3_out));
  LED S_9 (.in(nor_3_out));
  LED S_10 (.in(and_2_out));

  // Notes on the sheet:
  //   EQUIVALÊNCIA ENTRE BLOCOS
  //   EQUIVALÊNCIA "E" e "OU"
  //   EQUIVALÊNCIA "NAND" e "OU"
  //   EQUIVALÊNCIA "NOR" e "AND(entrada negada)"
  //   EQUIVALÊNCIA "OR" e "NAND(entrada negada)"
  //   S_3= E_3 . E_4
  //   ___
  //   ___
  //   ___
  //   S_4 = (E_5 + E_6)
  //   ___________
  //   S_5 = (E_7 . E_8)
  //   ___
  //   ___
  //   ___
  //   S_6 = E_9 + E_10
  //   S_7= E_11 + E_12
  //   ___________
  //   ___
  //   S_8 = (E_13 . E_14)
  //   S_9 = (E_15 . E_16)
  //   ___
  //   S_10 = E_17 + E_18
  //   ___________
  //   ___
  //   ___
  //   ___
  //   ___________
  //   ___
endmodule
