// Logisim project Expressoes_e_tabela_do_circuito (2).circ as structural Verilog: 1 circuit, main circuit main
module main (
  input  E_1,
  input  E_7,
  input  E_2,
  input  E_8,
  input  E_3,
  input  E_9,
  input  E_4,
  input  E_10,
  input  E_5,
  input  E_11,
  input  E_6,
  input  E_12,
  input  E_13,
  input  E_14,
  input  E_15,
  input  E_16,
  input  E_17,
  input  E_18,
  input  E_19,
  input  E_20,
  input  E_21,
  input  E_22
);

  wire and_1_out, and_2_out, and_3_out, and_4_out, and_5_out, and_6_out, and_7_out, and_8_out, and_9_out,
       or_1_out, or_2_out, or_3_out, or_4_out, or_5_out, or_6_out, or_7_out;

  and and_1 (and_1_out, E_1, E_2);
  and and_2 (and_2_out, E_13, E_14);
  or or_1 (or_1_out, E_16, E_17);
  and and_3 (and_3_out, E_4, E_5, E_6);
  LED S_2 (.in(and_3_out));
  and and_4 (and_4_out, ~E_19, E_20);  // AND_Gate
  and and_5 (and_5_out, ~E_20, E_19);  // AND_Gate
  and and_6 (and_6_out, ~E_21, ~E_22);  // AND_Gate
  and and_7 (and_7_out, E_22, E_21);
  and and_8 (and_8_out, and_1_out, E_3);
  or or_2 (or_2_out, and_2_out, E_15);
  and and_9 (and_9_out, or_1_out, E_18);
  or or_3 (or_3_out, and_6_out, and_7_out);
  LED S_1 (.in(and_8_out));
  LED S_5 (.in(or_2_out));
  LED S_6 (.in(and_9_out));
  or or_4 (or_4_out, and_4_out, and_5_out);
  LED S_7 (.in(or_4_out));
  LED S_8 (.in(or_3_out));
  or or_5 (or_5_out, E_7, E_8);
  or or_6 (or_6_out, E_10, E_11, E_12);
  or or_7 (or_7_out, or_5_out, E_9);
  LED S_4 (.in(or_6_out));
  LED S_3 (.in(or_7_out));

  // Notes on the sheet:
  //   CIRCUITOS COMBINACIONAIS
  //   EXPRESSÃO E TABELA A PARTIR DE CIRCUITO
  //   OU EXCLUSIVO "XOR"
  //   COENCIDENCIA "XNOR"
  //   S_1 = (E_1.E_2).E_3
  //   S_2 = (E_4 . E_5 . E_6)
  //   RESULTADO VERDADE IGUAIS FUNÇÕES SEMELHANTES POREM TEMPO DE PROPAGRAÇÃO DIFERENTE
  //   S_5 = (E_13.E_14)+E_15
  //   S_6 = (E_16+E_17).E_18
  //   ___
  //   ___
  //   S_7 = (E_19 . E_20) + ( E_19 . E_20)
  //   ___
  //   S_8 = (E_21 . E_22)+( E_21 . E_22)
  //   ___
  //   S_3 = (E_7+E_8)+E_9
  //   S_4 = (E_10 + E_11 + E_12
endmodule
