// Logisim project Unidade_de_Logica_e_Aritimetica.circ as structural Verilog
module ALU_1 (
  input  [7:0] E_1,
  input  [7:0] E_2,
  input  A1,
  input  A0,
  output [7:0] S_1
);

  wire dec2x4_1_o0, dec2x4_1_o1, dec2x4_1_o2, dec2x4_1_o3;
  wire [7:0] adder_1_out, divider_1_out, multiplier_1_out, subtractor_1_out;

  Adder adder_1 (.a(E_1), .b(E_2), .out(adder_1_out));  // open: cin, cout
  Subtractor subtractor_1 (.a(E_1), .b(E_2), .out(subtractor_1_out));  // open: bin, bout
  Multiplier multiplier_1 (.a(E_1), .b(E_2), .out(multiplier_1_out));  // open: cin, cout
  Divider divider_1 (.a(E_1), .b(E_2), .out(divider_1_out));  // open: upper, rem
  assign S_1 = dec2x4_1_o0 ? adder_1_out : 8'bz;  // Controlled_Buffer controlled_buffer_1
  assign S_1 = dec2x4_1_o1 ? subtractor_1_out : 8'bz;  // Controlled_Buffer controlled_buffer_2
  Dec2x4 dec2x4_1 (.A0(A1), .A1(A0), .O0(dec2x4_1_o0), .O1(dec2x4_1_o1), .O2(dec2x4_1_o2), .O3(dec2x4_1_o3));
  assign S_1 = dec2x4_1_o2 ? multiplier_1_out : 8'bz;  // Controlled_Buffer controlled_buffer_3
  assign S_1 = dec2x4_1_o3 ? divider_1_out : 8'bz;  // Controlled_Buffer controlled_buffer_4
  Hex_Digit_Display hex_digit_display_1 (.value(S_1[7:4]));  // open: dp
  Hex_Digit_Display hex_digit_display_2 (.value(S_1[3:0]));  // open: dp

  // Notes on the sheet:
  //   UNIDADE DE LÓGICA E ARITIMÉTICA - 1
endmodule

module Dec2x4 (
  input  A0,
  input  A1,
  output O0,
  output O1,
  output O2,
  output O3
);

  wire not_1_out, not_2_out;

  not not_1 (not_1_out, A0);
  not not_2 (not_2_out, A1);
  and and_1 (O0, not_1_out, not_2_out);
  and and_2 (O1, not_1_out, A1);
  and and_3 (O2, A0, not_2_out);
  and and_4 (O3, A0, A1);
endmodule

module ALU_2 (
  input  [7:0] E_1,
  input  [7:0] E_2,
  input  A2,
  input  A1,
  input  A0,
  output [7:0] S_1
);

  wire dec3x8_1_o0, dec3x8_1_o1, dec3x8_1_o2, dec3x8_1_o3, dec3x8_1_o4, dec3x8_1_o5, dec3x8_1_o6, dec3x8_1_o7;
  wire [7:0] adder_1_out, and_1_out, divider_1_out, multiplier_1_out, or_1_out, subtractor_1_out, xnor_1_out,
       xor_1_out;

  Adder adder_1 (.a(E_1), .b(E_2), .out(adder_1_out));  // open: cin, cout
  Subtractor subtractor_1 (.a(E_1), .b(E_2), .out(subtractor_1_out));  // open: bin, bout
  Multiplier multiplier_1 (.a(E_1), .b(E_2), .out(multiplier_1_out));  // open: cin, cout
  Divider divider_1 (.a(E_1), .b(E_2), .out(divider_1_out));  // open: upper, rem
  assign or_1_out = E_1 | E_2;  // OR_Gate or_1, 8 bits wide
  assign and_1_out = E_1 & E_2;  // AND_Gate and_1, 8 bits wide
  assign S_1 = dec3x8_1_o0 ? adder_1_out : 8'bz;  // Controlled_Buffer controlled_buffer_1
  assign S_1 = dec3x8_1_o1 ? subtractor_1_out : 8'bz;  // Controlled_Buffer controlled_buffer_2
  assign xor_1_out = E_1 ^ E_2;  // XOR_Gate xor_1, 8 bits wide
  assign xnor_1_out = ~(E_1 ^ E_2);  // XNOR_Gate xnor_1, 8 bits wide
  Dec3x8 dec3x8_1 (
    .A2(A2), .A1(A1), .A0(A0), .O0(dec3x8_1_o0), .O1(dec3x8_1_o1), .O2(dec3x8_1_o2), .O3(dec3x8_1_o3),
    .O4(dec3x8_1_o4), .O5(dec3x8_1_o5), .O6(dec3x8_1_o6), .O7(dec3x8_1_o7));
  assign S_1 = dec3x8_1_o2 ? multiplier_1_out : 8'bz;  // Controlled_Buffer controlled_buffer_3
  assign S_1 = dec3x8_1_o3 ? divider_1_out : 8'bz;  // Controlled_Buffer controlled_buffer_4
  assign S_1 = dec3x8_1_o4 ? or_1_out : 8'bz;  // Controlled_Buffer controlled_buffer_5
  assign S_1 = dec3x8_1_o5 ? and_1_out : 8'bz;  // Controlled_Buffer controlled_buffer_6
  assign S_1 = dec3x8_1_o6 ? xor_1_out : 8'bz;  // Controlled_Buffer controlled_buffer_7
  assign S_1 = dec3x8_1_o7 ? xnor_1_out : 8'bz;  // Controlled_Buffer controlled_buffer_8
  Hex_Digit_Display hex_digit_display_1 (.value(S_1[7:4]));  // open: dp
  Hex_Digit_Display hex_digit_display_2 (.value(S_1[3:0]));  // open: dp

  // Notes on the sheet:
  //   UNIDADE DE LÓGICA E ARITIMÉTICA - 2
endmodule

module Dec3x8 (
  input  A2,
  input  A1,
  input  A0,
  output O0,
  output O1,
  output O2,
  output O3,
  output O4,
  output O5,
  output O6,
  output O7
);

  wire not_1_out, not_2_out, not_3_out;

  not not_1 (not_1_out, A2);
  not not_2 (not_2_out, A1);
  not not_3 (not_3_out, A0);
  and and_1 (O0, not_1_out, not_2_out, not_3_out);
  and and_2 (O1, not_1_out, not_2_out, A0);
  and and_3 (O2, not_1_out, A1, not_3_out);
  and and_4 (O3, not_1_out, A1, A0);
  and and_5 (O4, A2, not_2_out, not_3_out);
  and and_6 (O5, A2, not_2_out, A0);
  and and_7 (O6, A2, A1, not_3_out);
  and and_8 (O7, A2, A1, A0);
endmodule
