// Logisim project f_x1_x2_x3_x4.circ as structural Verilog: 1 circuit, main circuit main
module main (
  input  X1,
  input  X2,
  input  X3,
  input  X4
);

  wire and_1_out, and_2_out, and_3_out, and_4_out, nand_1_out, nand_2_out, nand_3_out, nand_4_out,
       nand_5_out, not_1_out, not_2_out, not_3_out, not_4_out, or_1_out;

  not not_1 (not_1_out, X1);
  not not_2 (not_2_out, X2);
  not not_3 (not_3_out, X3);
  not not_4 (not_4_out, X4);
  nand nand_1 (nand_1_out, not_2_out, X3, not_4_out);
  nand nand_2 (nand_2_out, not_1_out, X2, not_3_out);
  nand nand_3 (nand_3_out, X1, X2);
  nand nand_4 (nand_4_out, X3, X4);
  nand nand_5 (nand_5_out, X2, X3);
  and and_1 (and_1_out, nand_1_out, X1);
  and and_2 (and_2_out, nand_2_out, X4);
  and and_3 (and_3_out, nand_3_out, nand_4_out);
  and and_4 (and_4_out, nand_5_out, not_1_out, not_4_out);
  or or_1 (or_1_out, and_1_out, and_2_out, and_3_out, and_4_out);
  // RGBLED rgbled_1: pin names not known; wires that end beside it: or_1_out

  // Notes on the sheet:
  //   _
  //   X1
  //   _
  //   X2
  //   _
  //   X3
  //   _
  //   X4
  //   f_x1_x2_x3_x4
endmodule
