// Digital circuit Bloco_e_(AND).dig as structural Verilog
module Bloco_e__AND (
  input  A1,
  input  B1
);

  wire A_b, and_1_out, B_b, relaydt_1_p4, relaydt_2_p3;

  Switch A (.A(1'b1), .B(A_b));
  Switch B (.A(1'b1), .B(B_b));
  // RelayDT relaydt_1: pin names not known; wires that end beside it: A_b, 1'b1, 1'b0, relaydt_1_p4
  and and_1 (and_1_out, A1, B1);
  // RelayDT relaydt_2: pin names not known; wires that end beside it: relaydt_1_p4, B_b, relaydt_2_p3, 1'b0
  LED S1 (.in(and_1_out));
  LED S (.in(relaydt_2_p3));

  // Notes on the sheet:
  //   BLOCO E ("AND")
endmodule
