// Digital circuit Bloco_inversor(NOT).dig as structural Verilog
module Bloco_inversor_NOT (
  input  A1
);

  wire A_b, not_1_out, relaydt_1_p4;

  Switch A (.A(1'b1), .B(A_b));
  // RelayDT relaydt_1: pin names not known; wires that end beside it: A_b, 1'b1, 1'b0, relaydt_1_p4
  not not_1 (not_1_out, A1);
  LED S1 (.in(not_1_out));
  LED S (.in(relaydt_1_p4));

  // Notes on the sheet:
  //   BLOCO INVERSOR ("NOT")
endmodule
