// Digital circuit Bloco_não_e_(NAND).dig as structural Verilog
module \Bloco_não_e__NAND  (
  input  A1,
  input  B1
);

  wire A_b, B_b, nand_1_out, relaydt_1_p4, relaydt_2_p3, relaydt_3_p2;

  Switch A (.A(1'b1), .B(A_b));
  Switch B (.A(1'b1), .B(B_b));
  // RelayDT relaydt_1: pin names not known; wires that end beside it: A_b, 1'b1, 1'b0, relaydt_1_p4
  nand nand_1 (nand_1_out, A1, B1);
  // RelayDT relaydt_2: pin names not known; wires that end beside it: relaydt_1_p4, B_b, relaydt_2_p3, 1'b0, relaydt_2_p3, 1'b0
  LED S1 (.in(nand_1_out));
  // RelayDT relaydt_3: pin names not known; wires that end beside it: 1'b1, relaydt_3_p2
  LED S (.in(relaydt_3_p2));

  // Notes on the sheet:
  //   BLOCO NÃO E ("NAND")
endmodule
