// Digital circuit Bloco_não_ou_(NOR).dig as structural Verilog
module \Bloco_não_ou__NOR  (
  input  A1,
  input  B1
);

  wire A_b, B_b, nor_1_out, relaydt_1_p3, relaydt_3_p2;

  Switch A (.A(1'b1), .B(A_b));
  Switch B (.A(1'b1), .B(B_b));
  // RelayDT relaydt_1: pin names not known; wires that end beside it: A_b, 1'b0, relaydt_1_p3
  // RelayDT relaydt_2: pin names not known; wires that end beside it: 1'b1, B_b, relaydt_1_p3, 1'b0, relaydt_1_p3, 1'b0
  nor nor_1 (nor_1_out, A1, B1);
  // RelayDT relaydt_3: pin names not known; wires that end beside it: 1'b1, relaydt_3_p2
  LED S1 (.in(nor_1_out));
  LED S (.in(relaydt_3_p2));

  // Notes on the sheet:
  //   BLOCO NÃO OU ("NOR")
endmodule
