// Digital circuit Bloco_ou_(OR).dig as structural Verilog
module Bloco_ou__OR (
  input  A1,
  input  B1
);

  wire A_b, B_b, or_1_out, relaydt_1_p3;

  Switch A (.A(1'b1), .B(A_b));
  Switch B (.A(1'b1), .B(B_b));
  // RelayDT relaydt_1: pin names not known; wires that end beside it: A_b, 1'b0, relaydt_1_p3
  // RelayDT relaydt_2: pin names not known; wires that end beside it: 1'b1, B_b, relaydt_1_p3, 1'b0
  or or_1 (or_1_out, A1, B1);
  LED S (.in(relaydt_1_p3));
  LED S1 (.in(or_1_out));

  // Notes on the sheet:
  //   BLOCO OU ("OR")
endmodule
