// Digital circuit Bloco_ou_exclusivo(XOR).dig as structural Verilog
module Bloco_ou_exclusivo_XOR (
  input  A1,
  input  B1
);

  wire A_b, B_b, relaydt_1_p4, relaydt_1_p5, relaydt_1_p7, xor_1_out;

  Switch A (.A(1'b1), .B(A_b));
  Switch B (.A(1'b1), .B(B_b));
  // RelayDT #(.poles(2)) relaydt_1: pin names not known; wires that end beside it: A_b, 1'b1, 1'b0, relaydt_1_p4, relaydt_1_p5, relaydt_1_p4, relaydt_1_p7
  xor xor_1 (xor_1_out, A1, B1);
  // RelayDT #(.poles(2)) relaydt_2: pin names not known; wires that end beside it: relaydt_1_p5, B_b, relaydt_1_p7, 1'b0
  LED S1 (.in(xor_1_out));
  LED S (.in(relaydt_1_p7));

  // Notes on the sheet:
  //   BLOCO OU EXCLUSIVO ("XOR")
endmodule
